# Fritzing sketch Automatic Dark sensing Light with Arduino and LRD (saved by Fritzing 0.8.7b)

parts:
  Part1 = Arduino Uno (Rev3)
  R1 = Resistor [tolerance=±5% resistance=220 package=THT]
  LED1 = LED - 5mm [color="Red (633nm)" package="5 mm [THT]"]
  R3 = Resistor [tolerance=±5% resistance=10k package=THT]
  LDR = Photocell (LDR) [package=THT]

nets:
  N1: Part1.A0, R3.Pin_0, LDR.pin_0
  N2: Part1.D8, R1.Pin_1
  N3: Part1.GND, LED1.cathode, R3.Pin_1
  N4: Part1.5V, LDR.pin_1
  N5: R1.Pin_0, LED1.anode
